# Fritzing sketch Temperature Alarm2 (saved by Fritzing 0.9.3b)
circuit board: 8.83163cm x 5.98237cm
breadboards: 1

parts:
  Part1 = Arduino Uno (Rev3)
  J1 = Piezo Speaker
  T1 = LM35 Temperature Sensor [package="TO92 [THT]"]

nets:
  N1: Part1.A0, T1.Vout
  GND: Part1.GND, J1.pin1, T1.GND
  N2: Part1.5V, T1.+Vs

notes:
  Buzzer
